// Logisim project DivisorCombinacional.circ as structural Verilog: 10 circuits, main circuit divisor_demo
module divisor_demo (
  input  [7:0] DIVIDENDO,
  input  [7:0] DIVISOR,
  output [7:0] QUOCIENTE,
  output [7:0] RESTO,
  output \DIVISÂO_POR_ZERO 
);

  // Probe on DIVIDENDO
  // Probe on DIVISOR
  divisor_combinacional Divisor_Inteiros (
    .DIVIDENDO(DIVIDENDO), .DIVISOR(DIVISOR), .RESTO(RESTO), .flag_dbz(\DIVISÂO_POR_ZERO ),
    .QUOCIENTE(QUOCIENTE));
  // Probe on QUOCIENTE
  // Probe on RESTO
endmodule

module divisor_combinacional (
  input  [7:0] DIVIDENDO,
  input  [7:0] DIVISOR,
  output [7:0] RESTO,
  output [7:0] QUOCIENTE,
  output flag_dbz
);

  wire xor_1_out;
  wire [7:0] adder_1_out, adder_2_out, adder_3_out, DVD, DVS, not_1_out, not_2_out, not_3_out,
       unidade0_1_aux_0, unidade1_1_aux_1, unidade2_1_aux_2, unidade3_1_aux_3, unidade4_1_aux_4,
       unidade5_1_aux_5, unidade6_1_aux_6, unidade7_1_quociente_0;

  assign not_1_out = ~DIVIDENDO;  // NOT_Gate not_1, 8 bits wide
  assign not_2_out = ~DIVISOR;  // NOT_Gate not_2, 8 bits wide
  Adder adder_1 (.a(not_1_out), .b(8'h1), .out(adder_1_out));  // open: cin, cout
  Adder adder_2 (.a(not_2_out), .b(8'h1), .out(adder_2_out));  // open: cin, cout
  Multiplexer #(.width(8), .enable("false")) multiplexer_1 (
    .in0(DIVIDENDO), .in1(adder_1_out), .out(DVD), .sel(DIVIDENDO[7]));
  // Probe on DVD
  Multiplexer #(.width(8), .enable("false")) multiplexer_2 (
    .in0(DIVISOR), .in1(adder_2_out), .out(DVS), .sel(DIVISOR[7]));
  // Probe on DVS
  xor xor_1 (xor_1_out, DIVIDENDO[7], DIVISOR[7]);
  unidade0 unidade0_1 (
    .DIVIDER(DVS), .QUOCIENTE_7(unidade7_1_quociente_0[7]), .AUX_0(unidade0_1_aux_0), .DIVIDEND(DVD));  // open: AUX_PREV
  nor nor_1 (flag_dbz, DIVISOR[0], DIVISOR[1], DIVISOR[2], DIVISOR[3], DIVISOR[4], DIVISOR[5], DIVISOR[6], DIVISOR[7]);
  unidade1 unidade1_1 (
    .AUX_PREV(unidade0_1_aux_0), .DIVIDER(DVS), .QUOCIENTE_6(unidade7_1_quociente_0[6]),
    .AUX_1(unidade1_1_aux_1), .DIVIDEND(DVD));
  unidade2 unidade2_1 (
    .AUX_PREV(unidade1_1_aux_1), .DIVIDER(DVS), .QUOCIENTE_5(unidade7_1_quociente_0[5]),
    .AUX_2(unidade2_1_aux_2), .DIVIDEND(DVD));
  unidade3 unidade3_1 (
    .AUX_PREV(unidade2_1_aux_2), .DIVIDER(DVS), .QUOCIENTE_4(unidade7_1_quociente_0[4]),
    .AUX_3(unidade3_1_aux_3), .DIVIDEND(DVD));
  unidade5 unidade5_1 (
    .AUX_PREV(unidade4_1_aux_4), .DIVIDER(DVS), .QUOCIENTE_2(unidade7_1_quociente_0[2]),
    .AUX_5(unidade5_1_aux_5), .DIVIDEND(DVD));
  unidade4 unidade4_1 (
    .AUX_PREV(unidade3_1_aux_3), .DIVIDER(DVS), .QUOCIENTE_3(unidade7_1_quociente_0[3]),
    .AUX_4(unidade4_1_aux_4), .DIVIDEND(DVD));
  unidade6 unidade6_1 (
    .AUX_PREV(unidade5_1_aux_5), .DIVIDER(DVS), .QUOCIENTE_1(unidade7_1_quociente_0[1]),
    .AUX_6(unidade6_1_aux_6), .DIVIDEND(DVD));
  unidade7 unidade7_1 (
    .AUX_PREV(unidade6_1_aux_6), .DIVIDER(DVS), .QUOCIENTE_0(unidade7_1_quociente_0[0]), .AUX_7(RESTO),
    .DIVIDEND(DVD));
  assign not_3_out = ~unidade7_1_quociente_0;  // NOT_Gate not_3, 8 bits wide
  Adder adder_3 (.a(not_3_out), .b(8'h1), .out(adder_3_out));  // open: cin, cout
  Multiplexer #(.width(8), .enable("false")) multiplexer_3 (
    .in0(unidade7_1_quociente_0), .in1(adder_3_out), .out(QUOCIENTE), .sel(xor_1_out));
  // Probe on RESTO
  // Probe on QUOCIENTE

  // Notes on the sheet:
  //   Comparação com zero
endmodule

module unidade0 (
  input  [7:0] AUX_PREV,
  input  [7:0] DIVIDEND,
  input  [7:0] DIVIDER,
  output [7:0] AUX_0,
  output QUOCIENTE_7
);

  wire subtractor_1_bout;
  wire [7:0] subtractor_1_out;

  // Probe on {{7{1'b0}}, DIVIDEND[7]}
  // Probe on DIVIDER
  Subtractor subtractor_1 (
    .a({{7{1'b0}}, DIVIDEND[7]}), .b(DIVIDER), .out(subtractor_1_out), .bout(subtractor_1_bout));  // open: bin
  not not_1 (QUOCIENTE_7, subtractor_1_bout);
  Multiplexer #(.width(8), .enable("false")) multiplexer_1 (
    .in0({{7{1'b0}}, DIVIDEND[7]}), .in1(subtractor_1_out), .out(AUX_0), .sel(QUOCIENTE_7));

  // Other names for the same wires on the sheet: DIV_7 = DIVIDEND[7]

  // Notes on the sheet:
  //   SUBTRATOR
endmodule

module unidade1 (
  input  [7:0] AUX_PREV,
  input  [7:0] DIVIDEND,
  input  [7:0] DIVIDER,
  output [7:0] AUX_1,
  output QUOCIENTE_6
);

  wire subtractor_1_bout;
  wire [7:0] subtractor_1_out;

  // Probe on {AUX_PREV[6:0], DIVIDEND[6]}
  // Probe on DIVIDER
  Subtractor subtractor_1 (
    .a({AUX_PREV[6:0], DIVIDEND[6]}), .b(DIVIDER), .out(subtractor_1_out), .bout(subtractor_1_bout));  // open: bin
  not not_1 (QUOCIENTE_6, subtractor_1_bout);
  Multiplexer #(.width(8), .enable("false")) multiplexer_1 (
    .in0({AUX_PREV[6:0], DIVIDEND[6]}), .in1(subtractor_1_out), .out(AUX_1), .sel(QUOCIENTE_6));

  // Other names for the same wires on the sheet: DIV_6 = DIVIDEND[6]

  // Notes on the sheet:
  //   SUBTRATOR
endmodule

module unidade2 (
  input  [7:0] AUX_PREV,
  input  [7:0] DIVIDEND,
  input  [7:0] DIVIDER,
  output [7:0] AUX_2,
  output QUOCIENTE_5
);

  wire subtractor_1_bout;
  wire [7:0] subtractor_1_out;

  // Probe on {AUX_PREV[6:0], DIVIDEND[5]}
  // Probe on DIVIDER
  Subtractor subtractor_1 (
    .a({AUX_PREV[6:0], DIVIDEND[5]}), .b(DIVIDER), .out(subtractor_1_out), .bout(subtractor_1_bout));  // open: bin
  not not_1 (QUOCIENTE_5, subtractor_1_bout);
  Multiplexer #(.width(8), .enable("false")) multiplexer_1 (
    .in0({AUX_PREV[6:0], DIVIDEND[5]}), .in1(subtractor_1_out), .out(AUX_2), .sel(QUOCIENTE_5));

  // Other names for the same wires on the sheet: DIV_5 = DIVIDEND[5]

  // Notes on the sheet:
  //   SUBTRATOR
endmodule

module unidade3 (
  input  [7:0] AUX_PREV,
  input  [7:0] DIVIDEND,
  input  [7:0] DIVIDER,
  output [7:0] AUX_3,
  output QUOCIENTE_4
);

  wire subtractor_1_bout;
  wire [7:0] subtractor_1_out;

  // Probe on {AUX_PREV[6:0], DIVIDEND[4]}
  // Probe on DIVIDER
  Subtractor subtractor_1 (
    .a({AUX_PREV[6:0], DIVIDEND[4]}), .b(DIVIDER), .out(subtractor_1_out), .bout(subtractor_1_bout));  // open: bin
  not not_1 (QUOCIENTE_4, subtractor_1_bout);
  Multiplexer #(.width(8), .enable("false")) multiplexer_1 (
    .in0({AUX_PREV[6:0], DIVIDEND[4]}), .in1(subtractor_1_out), .out(AUX_3), .sel(QUOCIENTE_4));

  // Other names for the same wires on the sheet: DIV_4 = DIVIDEND[4]

  // Notes on the sheet:
  //   SUBTRATOR
endmodule

module unidade4 (
  input  [7:0] AUX_PREV,
  input  [7:0] DIVIDEND,
  input  [7:0] DIVIDER,
  output [7:0] AUX_4,
  output QUOCIENTE_3
);

  wire subtractor_1_bout;
  wire [7:0] subtractor_1_out;

  // Probe on {AUX_PREV[6:0], DIVIDEND[3]}
  // Probe on DIVIDER
  Subtractor subtractor_1 (
    .a({AUX_PREV[6:0], DIVIDEND[3]}), .b(DIVIDER), .out(subtractor_1_out), .bout(subtractor_1_bout));  // open: bin
  not not_1 (QUOCIENTE_3, subtractor_1_bout);
  Multiplexer #(.width(8), .enable("false")) multiplexer_1 (
    .in0({AUX_PREV[6:0], DIVIDEND[3]}), .in1(subtractor_1_out), .out(AUX_4), .sel(QUOCIENTE_3));

  // Other names for the same wires on the sheet: DIV_3 = DIVIDEND[3]

  // Notes on the sheet:
  //   SUBTRATOR
endmodule

module unidade5 (
  input  [7:0] AUX_PREV,
  input  [7:0] DIVIDEND,
  input  [7:0] DIVIDER,
  output [7:0] AUX_5,
  output QUOCIENTE_2
);

  wire subtractor_1_bout;
  wire [7:0] subtractor_1_out;

  // Probe on {AUX_PREV[6:0], DIVIDEND[2]}
  // Probe on DIVIDER
  Subtractor subtractor_1 (
    .a({AUX_PREV[6:0], DIVIDEND[2]}), .b(DIVIDER), .out(subtractor_1_out), .bout(subtractor_1_bout));  // open: bin
  not not_1 (QUOCIENTE_2, subtractor_1_bout);
  Multiplexer #(.width(8), .enable("false")) multiplexer_1 (
    .in0({AUX_PREV[6:0], DIVIDEND[2]}), .in1(subtractor_1_out), .out(AUX_5), .sel(QUOCIENTE_2));

  // Other names for the same wires on the sheet: DIV_2 = DIVIDEND[2]

  // Notes on the sheet:
  //   SUBTRATOR
endmodule

module unidade6 (
  input  [7:0] AUX_PREV,
  input  [7:0] DIVIDEND,
  input  [7:0] DIVIDER,
  output [7:0] AUX_6,
  output QUOCIENTE_1
);

  wire subtractor_1_bout;
  wire [7:0] subtractor_1_out;

  // Probe on {AUX_PREV[6:0], DIVIDEND[1]}
  // Probe on DIVIDER
  Subtractor subtractor_1 (
    .a({AUX_PREV[6:0], DIVIDEND[1]}), .b(DIVIDER), .out(subtractor_1_out), .bout(subtractor_1_bout));  // open: bin
  not not_1 (QUOCIENTE_1, subtractor_1_bout);
  Multiplexer #(.width(8), .enable("false")) multiplexer_1 (
    .in0({AUX_PREV[6:0], DIVIDEND[1]}), .in1(subtractor_1_out), .out(AUX_6), .sel(QUOCIENTE_1));

  // Other names for the same wires on the sheet: DIV_1 = DIVIDEND[1]

  // Notes on the sheet:
  //   SUBTRATOR
endmodule

module unidade7 (
  input  [7:0] AUX_PREV,
  input  [7:0] DIVIDEND,
  input  [7:0] DIVIDER,
  output [7:0] AUX_7,
  output QUOCIENTE_0
);

  wire subtractor_1_bout;
  wire [7:0] subtractor_1_out;

  // Probe on {AUX_PREV[6:0], DIVIDEND[0]}
  // Probe on DIVIDER
  Subtractor subtractor_1 (
    .a({AUX_PREV[6:0], DIVIDEND[0]}), .b(DIVIDER), .out(subtractor_1_out), .bout(subtractor_1_bout));  // open: bin
  not not_1 (QUOCIENTE_0, subtractor_1_bout);
  Multiplexer #(.width(8), .enable("false")) multiplexer_1 (
    .in0({AUX_PREV[6:0], DIVIDEND[0]}), .in1(subtractor_1_out), .out(AUX_7), .sel(QUOCIENTE_0));

  // Other names for the same wires on the sheet: DIV_0 = DIVIDEND[0]

  // Notes on the sheet:
  //   SUBTRATOR
endmodule
