// Logisim project RaizQuadrada.circ as structural Verilog
module DataPath (
  input  MULTEn,
  input  NEn,
  input  GEn,
  input  CEn,
  input  CMUXSel,
  input  GMUXSel1,
  input  GMUXSel0,
  input  Clock,
  input  [31:0] InputNumber,
  output CEqualsZero,
  output MultGreaterThanN,
  output [31:0] G
);

  wire [31:0] C_q, MULT_q, multiplexer_1_out, multiplexer_2_out, multiplier_1_out, N_q, or_1_out,
       shifter_1_out, xor_1_out;

  Multiplexer #(.width(32), .enable("false")) multiplexer_1 (
    .in0(shifter_1_out), .in1(32'h8000), .out(multiplexer_1_out), .sel(CMUXSel));
  Multiplexer #(.select(2), .width(32), .enable("false")) multiplexer_2 (
    .in0(32'h8000), .in1(or_1_out), .in2(xor_1_out), .out(multiplexer_2_out), .sel({GMUXSel1, GMUXSel0}));  // open: in3
  Register #(.width(32)) C (.D(multiplexer_1_out), .en(CEn), .Q(C_q), .clk(Clock), .clr(1'b0));
  Register #(.width(32)) u_G (.D(multiplexer_2_out), .en(GEn), .Q(G), .clk(Clock), .clr(1'b0));
  Register #(.width(32)) N (.D(InputNumber), .en(NEn), .Q(N_q), .clk(Clock), .clr(1'b0));
  Shifter #(.width(32), .shift("ar")) shifter_1 (.in(C_q), .\dist (5'b00001), .out(shifter_1_out));
  assign xor_1_out = C_q ^ G;  // XOR_Gate xor_1, 32 bits wide
  assign or_1_out = C_q | G;  // OR_Gate or_1, 32 bits wide
  Comparator #(.width(32)) comparator_1 (.a({32{1'b0}}), .b(C_q), .eq(CEqualsZero));  // open: gt, lt
  Multiplier #(.width(32)) multiplier_1 (.a(G), .b(G), .out(multiplier_1_out));  // open: cin, cout
  Register #(.width(32)) MULT (.D(multiplier_1_out), .en(MULTEn), .Q(MULT_q), .clk(Clock), .clr(1'b0));
  Comparator #(.width(32), .mode("unsigned")) comparator_2 (
    .a(MULT_q), .b(N_q), .gt(MultGreaterThanN));  // open: eq, lt

  // Other names for the same wires on the sheet: CMUX = CMUXSel; GMUX[1:0] = {GMUXSel1, GMUXSel0}
endmodule

// CMUX
module ControlPath (
  input  CLOCK,
  input  RESET,
  input  CEqualsZero,
  input  MULTGreaterThanN,
  output MULTEn,
  output NEn,
  output GEn,
  output CEn,
  output CMUX,
  output GMUX1,
  output GMUX0,
  output DONE
);

  wire [2:0] CurrentState_q, NextState_q, nextstatelogic_1_nextstate0;

  Register #(.width(3)) NextState (
    .D(nextstatelogic_1_nextstate0), .en(1'b1), .Q(NextState_q), .clk(CLOCK), .clr(RESET));
  Register #(.width(3)) CurrentState (.D(NextState_q), .en(1'b1), .Q(CurrentState_q), .clk(CLOCK), .clr(RESET));
  OutputLogic outputlogic_1 (
    .currentState2(CurrentState_q[2]), .currentState1(CurrentState_q[1]), .currentState0(CurrentState_q[0]),
    .MULTEn(MULTEn), .NEn(NEn), .GEn(GEn), .CEn(CEn), .CMUX(CMUX), .GMUX1(GMUX1), .GMUX0(GMUX0), .Done(DONE));
  NextStateLogic nextstatelogic_1 (
    .currentState2(CurrentState_q[2]), .currentState1(CurrentState_q[1]), .currentState0(CurrentState_q[0]),
    .CEqZero(CEqualsZero), .MultGreaterThanN(MULTGreaterThanN), .nextState2(nextstatelogic_1_nextstate0[2]),
    .nextState1(nextstatelogic_1_nextstate0[1]), .nextState0(nextstatelogic_1_nextstate0[0]));

  // Notes on the sheet:
  //   OutputLogic
  //   NextStateLogic
endmodule

module NextStateLogic (
  input  currentState2,
  input  currentState1,
  input  currentState0,
  input  CEqZero,
  input  MultGreaterThanN,
  output nextState2,
  output nextState1,
  output nextState0
);

  wire and_1_out, and_2_out, and_3_out, and_4_out, and_5_out, and_6_out, and_7_out, and_8_out, not_1_out,
       not_2_out, not_3_out, not_4_out, not_5_out, not_6_out, not_7_out, not_8_out, not_9_out, not_10_out,
       not_11_out, not_12_out;

  not not_1 (not_1_out, currentState2);
  not not_2 (not_2_out, currentState1);
  not not_3 (not_3_out, currentState2);
  not not_4 (not_4_out, currentState1);
  not not_5 (not_5_out, currentState2);
  not not_6 (not_6_out, currentState0);
  not not_7 (not_7_out, currentState2);
  not not_8 (not_8_out, currentState0);
  not not_9 (not_9_out, currentState1);
  not not_10 (not_10_out, MultGreaterThanN);
  not not_11 (not_11_out, currentState2);
  not not_12 (not_12_out, currentState1);
  and and_1 (and_1_out, not_1_out, currentState1, currentState0);
  and and_2 (and_2_out, currentState2, not_2_out, currentState0);
  and and_3 (and_3_out, not_3_out, not_4_out, currentState0);
  and and_4 (and_4_out, not_5_out, currentState1, not_6_out);
  and and_5 (and_5_out, not_7_out, not_8_out);
  and and_6 (and_6_out, not_9_out, not_10_out);
  and and_7 (and_7_out, not_11_out, currentState1, CEqZero);
  and and_8 (and_8_out, currentState2, not_12_out);
  or or_1 (nextState2, and_1_out, and_2_out);
  or or_2 (nextState1, and_3_out, and_4_out);
  or or_3 (nextState0, and_5_out, and_6_out, and_7_out, and_8_out);
endmodule

module OutputLogic (
  input  currentState2,
  input  currentState1,
  input  currentState0,
  output MULTEn,
  output NEn,
  output GEn,
  output CEn,
  output CMUX,
  output GMUX1,
  output GMUX0,
  output Done
);

  wire and_3_out, and_4_out, and_5_out, and_6_out, not_1_out, not_2_out, not_3_out, not_4_out, not_5_out,
       not_6_out, not_7_out, not_8_out, not_9_out, not_10_out, not_11_out, not_12_out, not_13_out,
       not_14_out, not_15_out, not_16_out, not_17_out, not_18_out, not_19_out, not_20_out, not_21_out;

  not not_1 (not_1_out, currentState2);
  not not_2 (not_2_out, currentState1);
  not not_3 (not_3_out, currentState2);
  not not_4 (not_4_out, currentState1);
  not not_5 (not_5_out, currentState0);
  not not_6 (not_6_out, currentState2);
  not not_7 (not_7_out, currentState0);
  not not_8 (not_8_out, currentState1);
  not not_9 (not_9_out, currentState0);
  not not_10 (not_10_out, currentState2);
  not not_11 (not_11_out, currentState1);
  not not_12 (not_12_out, currentState0);
  not not_13 (not_13_out, currentState2);
  not not_14 (not_14_out, currentState2);
  not not_15 (not_15_out, currentState1);
  not not_16 (not_16_out, currentState0);
  not not_17 (not_17_out, currentState2);
  not not_18 (not_18_out, currentState0);
  not not_19 (not_19_out, currentState1);
  not not_20 (not_20_out, currentState0);
  not not_21 (not_21_out, currentState1);
  and and_1 (MULTEn, not_1_out, not_2_out, currentState0);
  and and_2 (NEn, not_3_out, not_4_out, not_5_out);
  and and_3 (and_3_out, not_6_out, not_7_out);
  and and_4 (and_4_out, not_8_out, not_9_out);
  and and_5 (and_5_out, not_10_out, not_11_out, not_12_out);
  and and_6 (and_6_out, not_13_out, currentState1, currentState0);
  and and_7 (CMUX, not_14_out, not_15_out, not_16_out);
  and and_8 (GMUX1, not_17_out, currentState1, not_18_out);
  and and_9 (GMUX0, currentState2, not_19_out, not_20_out);
  and and_10 (Done, currentState2, not_21_out, currentState0);
  or or_1 (GEn, and_3_out, and_4_out);
  or or_2 (CEn, and_5_out, and_6_out);
endmodule

module RaizQuadrada (
  input  [31:0] InputNumber,
  output [31:0] SqrtOfInputNumber,
  output CLOCK,
  output RESET,
  output DONE
);

  wire controlpath_1_cen, controlpath_1_cmux, controlpath_1_gen, controlpath_1_gmux0, controlpath_1_gmux1,
       controlpath_1_multen, controlpath_1_nen, datapath_1_cequalszero, datapath_1_multgreaterthann;

  ControlPath controlpath_1 (
    .CLOCK(CLOCK), .RESET(RESET), .MULTEn(controlpath_1_multen), .NEn(controlpath_1_nen),
    .GEn(controlpath_1_gen), .CEn(controlpath_1_cen), .CMUX(controlpath_1_cmux), .GMUX1(controlpath_1_gmux1),
    .GMUX0(controlpath_1_gmux0), .DONE(DONE), .CEqualsZero(datapath_1_cequalszero),
    .MULTGreaterThanN(datapath_1_multgreaterthann));
  DataPath datapath_1 (
    .InputNumber(InputNumber), .G(SqrtOfInputNumber), .CEqualsZero(datapath_1_cequalszero),
    .MultGreaterThanN(datapath_1_multgreaterthann), .MULTEn(controlpath_1_multen), .NEn(controlpath_1_nen),
    .GEn(controlpath_1_gen), .CEn(controlpath_1_cen), .CMUXSel(controlpath_1_cmux), .Clock(CLOCK),
    .GMUXSel1(controlpath_1_gmux1), .GMUXSel0(controlpath_1_gmux0));

  // Notes on the sheet:
  //   DataPath
  //   ControlPath
endmodule
